# Fritzing sketch e-stop (saved by Fritzing 1.0.6)
breadboards: 1

parts:
  LED1 = LED - 5mm [color="Red (633nm)" current=0.030A package="5 mm [THT]"]
  LED2 = LED - 5mm [color="Green (560nm)" current=0.030A part_number="5V LED" package="5 mm [THT]"]
  Pro_Micro1 = SparkFun Pro Micro
  R1 = Resistor [tolerance=±5% power=0.25W resistance=1k package=THT]
  S1 = Pushbutton [package=THT]

nets:
  N1: LED1.cathode, LED2.cathode, Pro_Micro1.GND, S1.leg0
  N2: LED1.anode, R1.Pin_1
  N3: LED2.anode, Pro_Micro1.14
  N4: Pro_Micro1.5, S1.leg1
  N5: Pro_Micro1.15, R1.Pin_0

custom parts:
  SparkFun Pro Micro: The Pro Micro is similar to the Pro Mini except with an ATmega32U4 on board. The USB transceiver inside the 32U4 allows us to add USB connectivity on-board and do away with bulky external USB interface. Based on: https://github.com/unorthodox-engineers/unorthodox-arduino/blob/master/Unorthodox/fritzing/parts/Pro%20Micro.fzpz
