# Fritzing sketch arduino_pwm_brushless_driver (saved by Fritzing 1.0.6)
breadboards: 1

parts:
  Uno1 = Arduino Uno (Rev3)
  R2 = Rotary Potentiometer (Small) [maximum_resistance=10kΩ knob_status=50% power=0.5W package=THT]
  R1 = Rotary Potentiometer (Small) [maximum_resistance=10kΩ knob_status=50% power=0.5W package=THT]
  Left_Dir = SPST Switch [package=ayz0202]
  Right_Dir = SPST Switch [package=ayz0202]

nets:
  N1: Uno1.A0, R2.leg2, R1.leg2
  N2: Uno1.A2, R2.wiper
  N3: Uno1.A3, R1.wiper
  N4: Uno1.A5/SCL, R2.leg1, R1.leg1
  N5: Uno1.D8, Left_Dir.S
  PWM Out Right (INV): Uno1.D9_PWM
  PWM Out Left: Uno1.D10_PWM/SS
  PWM Out Right: Uno1.D11_PWM/MOSI
  N6: Uno1.D3_PWM, Right_Dir.O
  N7: Uno1.D4, Right_Dir.S
  N8: Uno1.D5_PWM, Left_Dir.O
  PWM Out Left (INV): Uno1.D6_PWM
  N9: Uno1.D7, Left_Dir.P, Right_Dir.P
  5V/Power Left/Power Right: Uno1.5V
  GND/Ground Left/Ground Right: Uno1.GND
  12V: Uno1.VIN

notes:
  Left Speed
  Right Speed
  Fwd
  Rev
